# Fritzing sketch Digital_Sunglasses (saved by Fritzing 0.9.3b)
breadboards: 1

parts:
  Part1 = Arduino Nano (Rev3.0)
  R1 = Photocell (LDR) [package=THT]
  R2 = Photocell (LDR) [package=THT]
  J1 = Basic Servo
  R3 = 10k Ω Resistor [package=THT]
  R4 = 10k Ω Resistor [package=THT]

nets:
  GND: Part1.GND, J1.gnd, R3.Pin_0, R4.Pin_0
  N1: Part1.D3, J1.pulse
  5V: Part1.5V, R1.pin_1, R2.pin_1, J1.vcc
  N2: Part1.A1, R2.pin_0, R4.Pin_1
  N3: Part1.A0, R1.pin_0, R3.Pin_1

custom parts:
  10k Ω Resistor: A generic resistor (0.25W)
